# Fritzing sketch Lcd4ParPort (saved by Fritzing 0.9.4)
circuit board: 8.14089cm x 2.82446cm

parts:
  LCD1 = LCD screen
  J1 = Power Jack [package=power_jack_pth_lock]
  U1 = Mini-USB _B_ connector with 5th pin broken out. [package=usb-minib]
  D25 = DB25M
  R1 = Trimmer Potentiometer [maximum_resistance=10kΩ package=THT]
  J2 = Screw terminal - 2 pins [package=THT]
  Q1 = NPN-Transistor [package="TO92 [THT]"]
  R2 = Resistor [tolerance=±5% resistance=220 package=THT]

nets:
  GND: LCD1.VSS, J1.GND, U1.GND, R1.leg1, J2.pin1, Q1.E
  N1: LCD1.VDD, J1.PWR, U1.VBUS, R1.leg2, J2.pin2, R2.Pin_1
  N2: LCD1.V0, R1.wiper
  N3: LCD1.RS, D25.pin16
  N4: LCD1.R/W, D25.pin15
  N5: LCD1.E, D25.pin1
  N6: LCD1.DB0, D25.pin2
  N7: LCD1.DB1, D25.pin3
  N8: LCD1.DB2, D25.pin4
  N9: LCD1.DB3, D25.pin5
  N10: LCD1.DB4, D25.pin6
  N11: LCD1.DB5, D25.pin7
  N12: LCD1.DB6, D25.pin8
  N13: LCD1.DB7, D25.pin9
  N14: LCD1.LED+, R2.Pin_0
  N15: LCD1.LED-, Q1.C
  N16: D25.pin17, Q1.B
